// Logisim project g3-1.circ as structural Verilog: 3 circuits, main circuit main
module main (
  input  in_1
);

  wire and_1_out, clock, mips_alu_1_p4;
  wire [3:0] adder_1_p3;
  wire [4:0] multiplexer_2_out, multiplexer_3_out;
  wire [5:0] ALUControl_p2;
  wire [11:0] Control_p2;
  wire [27:0] adder_1_p3_2;
  wire [31:0] adder_2_p3, bit_extender_1_out_3, mips_alu_1_p5, mips_ram_1_p4, mipsprogramrom_1_p2,
       mipsprogramrom_1_p3, multiplexer_4_out, multiplexer_5_out, multiplexer_6_out, multiplexer_7_out,
       multiplexer_8_out, multiplexer_9_out, PC_q, registerfile_1_p6, registerfile_1_p7;

  Register #(.width(32)) PC (.D(multiplexer_8_out), .Q(PC_q), .clk(clock), .clr(in_1));  // open: en
  // Adder adder_1: pin names not known; wires that end beside it: 32'h4, PC_q, {adder_1_p3, adder_1_p3_2}
  Clock clock_1 (.out(clock));
  // MIPSProgramROM mipsprogramrom_1: pin names not known; wires that end beside it: PC_q, mipsprogramrom_1_p2, mipsprogramrom_1_p3, clock
  Multiplexer #(.width(32), .enable("false")) multiplexer_1 (
    .in0(multiplexer_9_out), .in1({adder_1_p3, adder_1_p3_2}), .out(mipsprogramrom_1_p3), .sel(Control_p2[11]));
  Multiplexer #(.width(5), .enable("false")) multiplexer_2 (
    .in0(mipsprogramrom_1_p2[20:16]), .in1(mipsprogramrom_1_p2[15:11]), .out(multiplexer_2_out),
    .sel(Control_p2[0]));
  Multiplexer #(.width(5), .enable("false")) multiplexer_3 (
    .in0(multiplexer_2_out), .in1({5{1'b1}}), .out(multiplexer_3_out), .sel(Control_p2[11]));
  // PLA Control: pin names not known; wires that end beside it: mipsprogramrom_1_p2[31:26], Control_p2
  // RegisterFile registerfile_1: pin names not known; wires that end beside it: Control_p2[1], multiplexer_3_out, mipsprogramrom_1_p2[25:21], mipsprogramrom_1_p2[20:16], in_1, registerfile_1_p6, registerfile_1_p7
  Bit_extender bit_extender_1 (.in_1(mipsprogramrom_1_p2[15:0]), .out_3(bit_extender_1_out_3), .in_2(Control_p2[2]));
  Multiplexer #(.width(32), .enable("false")) multiplexer_4 (
    .in0({adder_1_p3, adder_1_p3_2}), .in1(registerfile_1_p6), .out(multiplexer_4_out), .sel(ALUControl_p2[5]));
  Multiplexer #(.width(32), .enable("false")) multiplexer_5 (
    .in0(registerfile_1_p6), .in1({{27{1'b0}}, mipsprogramrom_1_p2[10:6]}), .out(multiplexer_5_out),
    .sel(ALUControl_p2[4]));
  Multiplexer #(.width(32), .enable("false")) multiplexer_6 (
    .in0(registerfile_1_p7), .in1(bit_extender_1_out_3), .out(multiplexer_6_out), .sel(Control_p2[6]));
  // PLA ALUControl: pin names not known; wires that end beside it: {Control_p2[5:3], mipsprogramrom_1_p2[5:0]}, ALUControl_p2
  // Adder adder_2: pin names not known; wires that end beside it: multiplexer_4_out, {bit_extender_1_out_3[29:0], 2'b00}, adder_2_p3
  // MIPS_ALU mips_alu_1: pin names not known; wires that end beside it: multiplexer_5_out, multiplexer_6_out, ALUControl_p2[3:0], mips_alu_1_p4, mips_alu_1_p5, mips_alu_1_p5[19:0], registerfile_1_p7, Control_p2[8]
  Multiplexer #(.width(32), .enable("false")) multiplexer_7 (
    .in0(multiplexer_4_out), .in1(adder_2_p3), .out(multiplexer_7_out), .sel(and_1_out));
  and and_1 (and_1_out, mips_alu_1_p4, Control_p2[7]);
  Multiplexer #(.width(32), .enable("false")) multiplexer_8 (
    .in0(multiplexer_7_out), .in1({adder_1_p3, mipsprogramrom_1_p2[25:0], 2'b00}), .out(multiplexer_8_out),
    .sel(Control_p2[10]));
  // MIPS_RAM mips_ram_1: pin names not known; wires that end beside it: Control_p2[9], clock, in_1, mips_ram_1_p4
  Multiplexer #(.width(32), .enable("false")) multiplexer_9 (
    .in0(mips_alu_1_p5), .in1(mips_ram_1_p4), .out(multiplexer_9_out), .sel(Control_p2[9]));

  // Other names for the same wires on the sheet: reset = in_1

  // Notes on the sheet:
  //   Enkeltcyklusarkitektur, vejledende løsning
  //   address
  //   rs
  //   rt
  //   rd
  //   immediate
  //   shamt
  //   funct
  //   opcode
  //   RegDst
  //   RegWrite
  //   JumpLink
  //   SignExt
  //   JumpR
  //   ALUOp
  //   Shamt
  //   ALUOp
  //   ALUSrc
  //   Branch
  //   Jump
  //   MemWrite
  //   MemRead
  //   MemRead
endmodule

module Bit_extender (
  input  [15:0] in_1,
  input  in_2,
  output [31:0] out_3
);

  wire [31:0] bit_extender_1_out, bit_extender_2_out;

  assign bit_extender_1_out = {{16{1'b0}}, in_1};  // Bit_Extender bit_extender_1
  assign bit_extender_2_out = {{16{in_1[15]}}, in_1};  // Bit_Extender bit_extender_2
  Multiplexer #(.width(32), .enable("false")) multiplexer_1 (
    .in0(bit_extender_1_out), .in1(bit_extender_2_out), .out(out_3), .sel(in_2));
endmodule

module Branch_prediction_table (
  input  [24:0] TagWrite,
  input  [1:0] PWrite,
  input  [31:0] TargetWrite,
  input  Clock,
  input  write,
  input  [4:0] IndexWrite,
  input  [4:0] Index,
  input  Clear,
  output [24:0] Tag,
  output [1:0] P,
  output [31:0] Target
);

  wire [31:27] registerfile_1_p1, registerfile_1_p7;

  // RegisterFile registerfile_1: pin names not known; wires that end beside it: {registerfile_1_p1, PWrite, TagWrite}, Clock, write, IndexWrite, Index, Clear, {registerfile_1_p7, P, Tag}
  // RegisterFile registerfile_2: pin names not known; wires that end beside it: TargetWrite, Clock, write, IndexWrite, Index, Clear, Target
endmodule
